// Logisim project cpuv2.circ as structural Verilog: 12 circuits, main circuit main3
module main (
  input  E_OUT,
  input  [3:0] OP_SELECT,
  input  [15:0] A,
  input  [15:0] B,
  output C,
  output V,
  output N,
  output [15:0] out_8,
  output Z
);

  wire [14:0] multiplexer_1_out;
  wire [15:0] adder_1_out, and_1_out, divider_1_out, multiplier_1_out, not_1_out, or_1_out, shifter_1_out,
       shifter_2_out, subtractor_1_out, xor_1_out;

  Adder #(.width(16)) adder_1 (.a(A), .b(B), .out(adder_1_out), .cout(C));  // open: cin
  Subtractor #(.width(16)) subtractor_1 (.a(A), .b(B), .out(subtractor_1_out));  // open: bin, bout
  Multiplier #(.width(16)) multiplier_1 (.a(A), .b(B), .out(multiplier_1_out));  // open: cin, cout
  Divider #(.width(16)) divider_1 (.a(A), .b(B), .out(divider_1_out));  // open: upper, rem
  assign not_1_out = ~A;  // NOT_Gate not_1, 16 bits wide
  Shifter #(.width(16)) shifter_1 (.in(A), .\dist (B[3:0]), .out(shifter_1_out));
  Shifter #(.width(16), .shift("lr")) shifter_2 (.in(A), .\dist (B[3:0]), .out(shifter_2_out));
  assign and_1_out = B & A;  // AND_Gate and_1, 16 bits wide
  assign or_1_out = B | A;  // OR_Gate or_1, 16 bits wide
  assign xor_1_out = B ^ A;  // XOR_Gate xor_1, 16 bits wide
  Multiplexer #(.select(4), .width(16), .enable("false")) multiplexer_1 (
    .in0(A), .in1(adder_1_out), .in2(subtractor_1_out), .in3(multiplier_1_out), .in4(divider_1_out),
    .in5(and_1_out), .in6(or_1_out), .in7(xor_1_out), .in8(not_1_out), .in9(shifter_1_out),
    .in10(shifter_2_out), .in11(B), .out({N, multiplexer_1_out}), .sel(OP_SELECT));  // open: in12, in13, in14, in15
  assign out_8 = E_OUT ? {N, multiplexer_1_out} : 16'bz;  // Controlled_Buffer controlled_buffer_1
  Comparator #(.width(16), .mode("unsigned")) comparator_1 (
    .a({N, multiplexer_1_out}), .b({16{1'b0}}), .eq(Z));  // open: gt, lt

  assign V = C;
endmodule

module main2 (
  input  [31:0] in_1,
  input  in_2,
  input  in_3,
  input  in_4
);

  wire clock_1_out, clock_2_out, comparator_1_eq, cpu_16b_1_meme, cpu_16b_1_mw;
  wire [15:0] cpu_16b_1_mema, cpu_16b_1_out_5, cpu_16b_1_pc, lcd_controller_1_out_5, lcd_controller_1_out_6,
       lcd_controller_1_out_7, lcd_controller_1_out_8, lcd_controller_1_out_9, lcd_controller_1_out_10,
       lcd_controller_1_out_11, lcd_controller_1_out_12, lcd_controller_1_out_13, lcd_controller_1_out_14,
       lcd_controller_1_out_15, lcd_controller_1_out_16, lcd_controller_1_out_17, lcd_controller_1_out_18,
       lcd_controller_1_out_19, lcd_controller_1_out_20;
  wire [31:0] multiplexer_1_out, rom_1_data;

  Register register_1 ();  // open: D, en, Q, clk, clr
  Clock clock_1 (.out(clock_1_out));
  Multiplexer #(.width(32), .enable("false")) multiplexer_1 (
    .in0(rom_1_data), .in1(in_1), .out(multiplexer_1_out), .sel(in_2));
  ROM #(.addrWidth(16), .dataWidth(32)) rom_1 (.addr(cpu_16b_1_pc), .data(rom_1_data));
  CPU_16b cpu_16b_1 (
    .INSTRUCTION(multiplexer_1_out), .CLK(clock_1_out), .RST(in_4), .MEMA(cpu_16b_1_mema), .PC(cpu_16b_1_pc),
    .MW(cpu_16b_1_mw), .MEME(cpu_16b_1_meme), .out_5(cpu_16b_1_out_5));
  RAM #(.addrWidth(16), .dataWidth(16)) ram_1 (
    .addr(cpu_16b_1_mema), .we(cpu_16b_1_mw), .oe(cpu_16b_1_meme), .clk(clock_1_out), .data(cpu_16b_1_out_5));
  DotMatrix #(.matrixcols(16), .matrixrows(16)) dotmatrix_1 (
    .col0(lcd_controller_1_out_5), .col1(lcd_controller_1_out_9), .col2(lcd_controller_1_out_13),
    .col3(lcd_controller_1_out_17), .col4(lcd_controller_1_out_6), .col5(lcd_controller_1_out_10),
    .col6(lcd_controller_1_out_14), .col7(lcd_controller_1_out_18), .col8(lcd_controller_1_out_7),
    .col9(lcd_controller_1_out_11), .col10(lcd_controller_1_out_15), .col11(lcd_controller_1_out_19),
    .col12(lcd_controller_1_out_8), .col13(lcd_controller_1_out_12), .col14(lcd_controller_1_out_16),
    .col15(lcd_controller_1_out_20));
  LCD_CONTROLLER lcd_controller_1 (
    .D(cpu_16b_1_out_5), .E(comparator_1_eq), .ADD(cpu_16b_1_mema[1:0]), .in_4(clock_2_out),
    .out_5(lcd_controller_1_out_5), .out_9(lcd_controller_1_out_9), .out_13(lcd_controller_1_out_13),
    .out_17(lcd_controller_1_out_17), .out_6(lcd_controller_1_out_6), .out_10(lcd_controller_1_out_10),
    .out_14(lcd_controller_1_out_14), .out_18(lcd_controller_1_out_18), .out_7(lcd_controller_1_out_7),
    .out_11(lcd_controller_1_out_11), .out_15(lcd_controller_1_out_15), .out_19(lcd_controller_1_out_19),
    .out_8(lcd_controller_1_out_8), .out_12(lcd_controller_1_out_12), .out_16(lcd_controller_1_out_16),
    .out_20(lcd_controller_1_out_20));
  Clock clock_2 (.out(clock_2_out));
  Comparator #(.width(14)) comparator_1 (
    .a(cpu_16b_1_mema[15:2]), .b({14{1'b1}}), .eq(comparator_1_eq));  // open: gt, lt

  // Notes on the sheet:
  //   contents of rom_1 (hex, n*v repeats v):
  //   81820111 81810111 81810ef2 218f000a 9102001f 238f0001 818b0100 81820111 81810001 218f0001 c180fffc
  //   c181fffd 818b0203 c182fffe 1800fe0
endmodule

module RegisterFile (
  input  CLK,
  input  WE,
  input  [3:0] SD,
  input  [15:0] DATA,
  input  in_5,
  input  [3:0] SA,
  input  [3:0] SB,
  output [15:0] PC,
  output [15:0] A,
  output [15:0] B
);

  wire decoder_1_out0, decoder_1_out1, decoder_1_out2, decoder_1_out3, decoder_1_out4, decoder_1_out5,
       decoder_1_out6, decoder_1_out7, decoder_1_out8, decoder_1_out9, decoder_1_out10, decoder_1_out11,
       decoder_1_out12, decoder_1_out13, decoder_1_out14, decoder_1_out15;
  wire [15:0] r00_q, r01_q, r02_q, r03_q, r04_q, r05_q, r06_q, r07_q, r08_q, r09_q, r10_q, r11_q, r12_q,
       r13_q, r14_q;

  Register #(.width(16), .trigger("high")) r00 (.D(DATA), .en(decoder_1_out0), .clk(CLK), .Q(r00_q), .clr(in_5));
  Register #(.width(16), .trigger("high")) r01 (.D(DATA), .en(decoder_1_out1), .clk(CLK), .Q(r01_q), .clr(in_5));
  Register #(.width(16), .trigger("high")) r02 (.D(DATA), .en(decoder_1_out2), .clk(CLK), .Q(r02_q), .clr(in_5));
  Register #(.width(16), .trigger("high")) r03 (.D(DATA), .en(decoder_1_out3), .clk(CLK), .Q(r03_q), .clr(in_5));
  Decoder #(.select(4)) decoder_1 (
    .out0(decoder_1_out0), .out1(decoder_1_out1), .out2(decoder_1_out2), .out3(decoder_1_out3),
    .out4(decoder_1_out4), .out5(decoder_1_out5), .out6(decoder_1_out6), .out7(decoder_1_out7),
    .out8(decoder_1_out8), .out9(decoder_1_out9), .out10(decoder_1_out10), .out11(decoder_1_out11),
    .out12(decoder_1_out12), .out13(decoder_1_out13), .out14(decoder_1_out14), .out15(decoder_1_out15),
    .sel(SD), .en(WE));
  Register #(.width(16), .trigger("high")) r04 (.D(DATA), .en(decoder_1_out4), .clk(CLK), .Q(r04_q), .clr(in_5));
  Register #(.width(16), .trigger("high")) r05 (.D(DATA), .en(decoder_1_out5), .clk(CLK), .Q(r05_q), .clr(in_5));
  Register #(.width(16), .trigger("high")) r06 (.D(DATA), .en(decoder_1_out6), .clk(CLK), .Q(r06_q), .clr(in_5));
  Register #(.width(16), .trigger("high")) r07 (.D(DATA), .en(decoder_1_out7), .clk(CLK), .Q(r07_q), .clr(in_5));
  Multiplexer #(.select(4), .width(16), .enable("false")) multiplexer_1 (
    .in0(r00_q), .in1(r01_q), .in2(r02_q), .in3(r03_q), .in4(r04_q), .in5(r05_q), .in6(r06_q), .in7(r07_q),
    .in8(r08_q), .in9(r09_q), .in10(r10_q), .in11(r11_q), .in12(r12_q), .in13(r13_q), .in14(r14_q),
    .in15(PC), .out(A), .sel(SA));
  Register #(.width(16), .trigger("high")) r08 (.D(DATA), .en(decoder_1_out8), .clk(CLK), .Q(r08_q), .clr(in_5));
  Register #(.width(16), .trigger("high")) r09 (.D(DATA), .en(decoder_1_out9), .clk(CLK), .Q(r09_q), .clr(in_5));
  Register #(.width(16), .trigger("high")) r10 (.D(DATA), .en(decoder_1_out10), .clk(CLK), .Q(r10_q), .clr(in_5));
  Register #(.width(16), .trigger("high")) r11 (.D(DATA), .en(decoder_1_out11), .clk(CLK), .Q(r11_q), .clr(in_5));
  Multiplexer #(.select(4), .width(16), .enable("false")) multiplexer_2 (
    .in0(r00_q), .in1(r01_q), .in2(r02_q), .in3(r03_q), .in4(r04_q), .in5(r05_q), .in6(r06_q), .in7(r07_q),
    .in8(r08_q), .in9(r09_q), .in10(r10_q), .in11(r11_q), .in12(r12_q), .in13(r13_q), .in14(r14_q),
    .in15(PC), .out(B), .sel(SB));
  Register #(.width(16), .trigger("high")) r12 (.D(DATA), .en(decoder_1_out12), .clk(CLK), .Q(r12_q), .clr(in_5));
  Register #(.width(16), .trigger("high")) r13 (.D(DATA), .en(decoder_1_out13), .clk(CLK), .Q(r13_q), .clr(in_5));
  Register #(.width(16), .trigger("high")) r14 (.D(DATA), .en(decoder_1_out14), .clk(CLK), .Q(r14_q), .clr(in_5));
  PC_REG pc_reg_1 (.RST(in_5), .in_2(DATA), .WE(decoder_1_out15), .CLK(CLK), .Q(PC));
endmodule

module Instruction_decoder (
  input  [3:0] Flags,
  input  [31:0] INSTRUCTION_IN,
  output out_3,
  output [3:0] SB,
  output MB,
  output [3:0] SA,
  output [3:0] SD,
  output MD,
  output [7:0] IMM,
  output MI,
  output MS,
  output [15:0] out_12,
  output MA,
  output MW,
  output RW,
  output [3:0] OP
);

  wire and_1_out, and_2_out, not_1_out, not_2_out, not_3_out, or_1_out;
  wire [3:0] multiplexer_1_out;
  wire [26:24] multiplexer_1_out_2;

  Multiplexer #(.width(32), .enable("false")) multiplexer_1 (
    .in0(INSTRUCTION_IN), .in1({32{1'b0}}),
    .out({MB, MD, MI, MS, MA, multiplexer_1_out_2, multiplexer_1_out, OP, IMM[7:4], out_12[11:4], IMM[3:0]}),
    .sel(1'b0));
  CONDITION_BOX condition_box_1 (
    .Z(Flags[3]), .C(Flags[2]), .V(Flags[1]), .N(Flags[0]), .CS(multiplexer_1_out_2), .CT(out_3));
  and and_1 (and_1_out, MW, not_1_out);
  not not_1 (not_1_out, MA);
  Multiplexer #(.width(4), .enable("false")) multiplexer_2 (.in0(out_12[7:4]), .in1(OP), .out(SA), .sel(and_1_out));
  Multiplexer #(.width(4), .enable("false")) multiplexer_3 (.in0(out_12[11:8]), .in1(OP), .out(SD), .sel(or_1_out));
  or or_1 (or_1_out, MI, and_2_out);
  and and_2 (and_2_out, not_2_out, MD);
  not not_2 (not_2_out, MB);
  and and_3 (MW, MB, MD);
  not not_3 (not_3_out, MW);
  and and_4 (RW, not_3_out, multiplexer_1_out[3]);

  assign {out_12[15:12], out_12[3:0]} = IMM;
  assign SB = IMM[3:0];
endmodule

module CONDITION_BOX (
  input  Z,
  input  C,
  input  V,
  input  N,
  input  [2:0] CS,
  output CT
);

  wire and_1_out, not_1_out, not_2_out;

  not not_1 (not_1_out, Z);
  and and_1 (and_1_out, not_1_out, N);
  not not_2 (not_2_out, Z);
  Multiplexer #(.select(3), .enable("false")) multiplexer_1 (
    .in0(1'b0), .in1(1'b1), .in2(Z), .in3(not_2_out), .in4(and_1_out), .out(CT), .sel(CS));  // open: in5, in6, in7
endmodule

module CPU_16b (
  input  [31:0] INSTRUCTION,
  input  CLK,
  input  RST,
  output MEME,
  output [15:0] out_5,
  output [15:0] MEMA,
  output [15:0] PC,
  output MW
);

  wire and_1_out, instruction_decoder_1_ma, instruction_decoder_1_mb, instruction_decoder_1_md,
       instruction_decoder_1_mi, instruction_decoder_1_ms, instruction_decoder_1_out_3,
       instruction_decoder_1_rw, not_1_out, not_2_out, or_1_out;
  wire [3:0] instruction_decoder_1_op, instruction_decoder_1_sa, instruction_decoder_1_sb,
       instruction_decoder_1_sd, main_1_n, multiplexer_3_out, register_1_q;
  wire [7:0] instruction_decoder_1_imm;
  wire [15:0] controlled_buffer_1_out, instruction_decoder_1_out_12, main_1_out_8, multiplexer_1_out,
       multiplexer_2_out, multiplexer_4_out, register_2_q, registerfile_1_a, registerfile_1_b;

  Instruction_decoder instruction_decoder_1 (
    .INSTRUCTION_IN(INSTRUCTION), .MB(instruction_decoder_1_mb), .MD(instruction_decoder_1_md),
    .MI(instruction_decoder_1_mi), .MS(instruction_decoder_1_ms), .MW(MW), .RW(instruction_decoder_1_rw),
    .SB(instruction_decoder_1_sb), .SA(instruction_decoder_1_sa), .SD(instruction_decoder_1_sd),
    .IMM(instruction_decoder_1_imm), .out_12(instruction_decoder_1_out_12), .OP(instruction_decoder_1_op),
    .Flags(register_1_q), .out_3(instruction_decoder_1_out_3), .MA(instruction_decoder_1_ma));
  Register #(.width(4), .trigger("falling")) register_1 (
    .D(main_1_n), .en(instruction_decoder_1_ms), .clk(CLK), .Q(register_1_q), .clr(RST));
  and and_1 (and_1_out, instruction_decoder_1_out_3, instruction_decoder_1_rw);
  RegisterFile registerfile_1 (
    .WE(and_1_out), .SD(instruction_decoder_1_sd), .DATA(register_2_q), .SA(instruction_decoder_1_sa),
    .SB(instruction_decoder_1_sb), .A(registerfile_1_a), .B(registerfile_1_b), .PC(PC), .CLK(CLK), .in_5(RST));
  Multiplexer #(.width(16), .enable("false")) multiplexer_1 (
    .in0(registerfile_1_a), .in1(instruction_decoder_1_out_12), .out(multiplexer_1_out),
    .sel(instruction_decoder_1_mi));
  Multiplexer #(.width(16), .enable("false")) multiplexer_2 (
    .in0(registerfile_1_b), .in1({{8{1'b0}}, instruction_decoder_1_imm}), .out(multiplexer_2_out),
    .sel(instruction_decoder_1_mb));
  Multiplexer #(.width(4), .enable("false")) multiplexer_3 (
    .in0(instruction_decoder_1_op), .in1(4'b0000), .out(multiplexer_3_out), .sel(or_1_out));
  or or_1 (or_1_out, instruction_decoder_1_md, instruction_decoder_1_mi, MW);
  not not_1 (not_1_out, instruction_decoder_1_mb);
  and and_2 (MEME, instruction_decoder_1_md, not_1_out);
  Register #(.width(16)) register_2 (.D(multiplexer_4_out), .en(1'b1), .clk(CLK), .Q(register_2_q), .clr(RST));
  assign controlled_buffer_1_out = MEME ? out_5 : 16'bz;  // Controlled_Buffer controlled_buffer_1
  main main_1 (
    .E_OUT(instruction_decoder_1_out_3), .OP_SELECT(multiplexer_3_out), .A(multiplexer_1_out),
    .B(multiplexer_2_out), .C(main_1_n[2]), .V(main_1_n[1]), .N(main_1_n[0]), .out_8(main_1_out_8),
    .Z(main_1_n[3]));
  Multiplexer #(.width(16), .enable("false")) multiplexer_4 (
    .in0(main_1_out_8), .in1(controlled_buffer_1_out), .out(multiplexer_4_out), .sel(MEME));
  assign out_5 = not_2_out ? main_1_out_8 : 16'bz;  // Controlled_Buffer controlled_buffer_2
  not not_2 (not_2_out, MEME);
  Multiplexer #(.width(16), .enable("false")) multiplexer_5 (
    .in0(instruction_decoder_1_out_12), .in1(multiplexer_1_out), .out(MEMA), .sel(instruction_decoder_1_ma));
endmodule

module PC_REG (
  input  RST,
  input  [15:0] in_2,
  input  WE,
  input  CLK,
  output [15:0] Q
);

  wire [15:0] adder_1_out, multiplexer_1_out;

  Adder #(.width(16)) adder_1 (.a(16'h1), .b(Q), .out(adder_1_out));  // open: cin, cout
  Multiplexer #(.width(16), .enable("false")) multiplexer_1 (
    .in0(adder_1_out), .in1(in_2), .out(multiplexer_1_out), .sel(WE));
  Register #(.width(16), .trigger("falling")) PC (.D(multiplexer_1_out), .en(1'b1), .clk(CLK), .Q(Q), .clr(RST));
endmodule

module LCD_CONTROLLER (
  input  [15:0] D,
  input  E,
  input  [1:0] ADD,
  input  in_4,
  output [15:0] out_5,
  output [15:0] out_6,
  output [15:0] out_7,
  output [15:0] out_8,
  output [15:0] out_9,
  output [15:0] out_10,
  output [15:0] out_11,
  output [15:0] out_12,
  output [15:0] out_13,
  output [15:0] out_14,
  output [15:0] out_15,
  output [15:0] out_16,
  output [15:0] out_17,
  output [15:0] out_18,
  output [15:0] out_19,
  output [15:0] out_20
);

  wire decoder_1_out0, decoder_1_out1, decoder_1_out2, or_1_out;
  wire [15:0] b_changer_1_out, COL_REG_q, decoder_2_out0, multiplexer_1_out, register_1_q, ROW_REG_q;

  Decoder #(.select(2)) decoder_1 (
    .out0(decoder_1_out0), .out1(decoder_1_out1), .out2(decoder_1_out2), .sel(ADD), .en(E));  // open: out3
  Register #(.width(16)) ROW_REG (.D(D), .en(decoder_1_out0), .clk(in_4), .Q(ROW_REG_q));  // open: clr
  Decoder #(.select(4)) decoder_2 (
    .out0(decoder_2_out0[0]), .out1(decoder_2_out0[1]), .out2(decoder_2_out0[2]), .out3(decoder_2_out0[3]),
    .out4(decoder_2_out0[4]), .out5(decoder_2_out0[5]), .out6(decoder_2_out0[6]), .out7(decoder_2_out0[7]),
    .out8(decoder_2_out0[8]), .out9(decoder_2_out0[9]), .out10(decoder_2_out0[10]),
    .out11(decoder_2_out0[11]), .out12(decoder_2_out0[12]), .out13(decoder_2_out0[13]),
    .out14(decoder_2_out0[14]), .out15(decoder_2_out0[15]), .sel(ROW_REG_q[3:0]));  // open: en
  Register #(.width(16)) COL_REG (.D(D), .en(decoder_1_out1), .clk(in_4), .Q(COL_REG_q));  // open: clr
  // NOT_Gate not_1 has open pins: in=in_4, out=open
  Register #(.width(16)) register_1 (.D(D), .en(decoder_1_out2), .clk(in_4), .Q(register_1_q), .clr(or_1_out));
  Multiplexer #(.select(4), .width(16), .enable("false")) multiplexer_1 (
    .in0(out_5), .in1(out_9), .in2(out_13), .in3(out_17), .in4(out_6), .in5(out_10), .in6(out_14),
    .in7(out_18), .in8(out_7), .in9(out_11), .in10(out_15), .in11(out_19), .in12(out_8), .in13(out_12),
    .in14(out_16), .in15(out_20), .out(multiplexer_1_out), .sel(COL_REG_q[3:0]));
  B_Changer b_changer_1 (
    .DATA(multiplexer_1_out), .Change_bit(decoder_2_out0), .C_type(register_1_q[0]), .OUT(b_changer_1_out));
  or or_1 (or_1_out, register_1_q[1], register_1_q[2], register_1_q[0]);
  DotMatrix #(.matrixcols(16), .matrixrows(16)) dotmatrix_1 (
    .col0(out_5), .col1(out_9), .col2(out_13), .col3(out_17), .col4(out_6), .col5(out_10), .col6(out_14),
    .col7(out_18), .col8(out_7), .col9(out_11), .col10(out_15), .col11(out_19), .col12(out_8),
    .col13(out_12), .col14(out_16), .col15(out_20));
  reg_16x16 reg_16x16_1 (
    .in_1(1'b1), .in_2(COL_REG_q[3:0]), .in_3(register_1_q[1]), .in_4(register_1_q[2]),
    .in_5(b_changer_1_out), .out_6(out_5), .out_7(out_6), .out_8(out_7), .out_9(out_8), .out_10(out_9),
    .out_11(out_10), .out_12(out_11), .out_13(out_12), .out_14(out_13), .out_15(out_14), .out_16(out_15),
    .out_17(out_16), .out_18(out_17), .out_19(out_18), .out_20(out_19), .out_21(out_20));

  // Other names for the same wires on the sheet: r0[15:0] = out_5; r1[15:0] = out_9; r2[15:0] = out_13;
  //   r3[15:0] = out_17; r4[15:0] = out_6; r5[15:0] = out_10; r6[15:0] = out_14; r7[15:0] = out_18; r8[15:0] = out_7;
  //   r9[15:0] = out_11; r10[15:0] = out_15; r11[15:0] = out_19; r12[15:0] = out_8; r13[15:0] = out_12;
  //   r14[15:0] = out_16; r15[15:0] = out_20
endmodule

module reg_16x16 (
  input  in_1,
  input  [3:0] in_2,
  input  in_3,
  input  in_4,
  input  [15:0] in_5,
  output [15:0] out_6,
  output [15:0] out_7,
  output [15:0] out_8,
  output [15:0] out_9,
  output [15:0] out_10,
  output [15:0] out_11,
  output [15:0] out_12,
  output [15:0] out_13,
  output [15:0] out_14,
  output [15:0] out_15,
  output [15:0] out_16,
  output [15:0] out_17,
  output [15:0] out_18,
  output [15:0] out_19,
  output [15:0] out_20,
  output [15:0] out_21
);

  wire decoder_1_out0, decoder_1_out1, decoder_1_out2, decoder_1_out3, decoder_1_out4, decoder_1_out5,
       decoder_1_out6, decoder_1_out7, decoder_1_out8, decoder_1_out9, decoder_1_out10, decoder_1_out11,
       decoder_1_out12, decoder_1_out13, decoder_1_out14, decoder_1_out15;

  Register #(.width(16), .trigger("falling")) register_1 (
    .D(in_5), .en(decoder_1_out0), .clk(in_3), .Q(out_6), .clr(in_4));
  Register #(.width(16), .trigger("falling")) register_2 (
    .D(in_5), .en(decoder_1_out1), .clk(in_3), .Q(out_10), .clr(in_4));
  Register #(.width(16), .trigger("falling")) register_3 (
    .D(in_5), .en(decoder_1_out2), .clk(in_3), .Q(out_14), .clr(in_4));
  Register #(.width(16), .trigger("falling")) register_4 (
    .D(in_5), .en(decoder_1_out3), .clk(in_3), .Q(out_18), .clr(in_4));
  Register #(.width(16), .trigger("falling")) register_5 (
    .D(in_5), .en(decoder_1_out4), .clk(in_3), .Q(out_7), .clr(in_4));
  Register #(.width(16), .trigger("falling")) register_6 (
    .D(in_5), .en(decoder_1_out5), .clk(in_3), .Q(out_11), .clr(in_4));
  Register #(.width(16), .trigger("falling")) register_7 (
    .D(in_5), .en(decoder_1_out6), .clk(in_3), .Q(out_15), .clr(in_4));
  Register #(.width(16), .trigger("falling")) register_8 (
    .D(in_5), .en(decoder_1_out7), .clk(in_3), .Q(out_19), .clr(in_4));
  Decoder #(.select(4)) decoder_1 (
    .out0(decoder_1_out0), .out1(decoder_1_out1), .out2(decoder_1_out2), .out3(decoder_1_out3),
    .out4(decoder_1_out4), .out5(decoder_1_out5), .out6(decoder_1_out6), .out7(decoder_1_out7),
    .out8(decoder_1_out8), .out9(decoder_1_out9), .out10(decoder_1_out10), .out11(decoder_1_out11),
    .out12(decoder_1_out12), .out13(decoder_1_out13), .out14(decoder_1_out14), .out15(decoder_1_out15),
    .sel(in_2), .en(in_1));
  Register #(.width(16), .trigger("falling")) register_9 (
    .D(in_5), .en(decoder_1_out8), .clk(in_3), .Q(out_8), .clr(in_4));
  Register #(.width(16), .trigger("falling")) register_10 (
    .D(in_5), .en(decoder_1_out9), .clk(in_3), .Q(out_12), .clr(in_4));
  Register #(.width(16), .trigger("falling")) register_11 (
    .D(in_5), .en(decoder_1_out10), .clk(in_3), .Q(out_16), .clr(in_4));
  Register #(.width(16), .trigger("falling")) register_12 (
    .D(in_5), .en(decoder_1_out11), .clk(in_3), .Q(out_20), .clr(in_4));
  Register #(.width(16), .trigger("falling")) register_13 (
    .D(in_5), .en(decoder_1_out12), .clk(in_3), .Q(out_9), .clr(in_4));
  Register #(.width(16), .trigger("falling")) register_14 (
    .D(in_5), .en(decoder_1_out13), .clk(in_3), .Q(out_13), .clr(in_4));
  Register #(.width(16), .trigger("falling")) register_15 (
    .D(in_5), .en(decoder_1_out14), .clk(in_3), .Q(out_17), .clr(in_4));
  Register #(.width(16), .trigger("falling")) register_16 (
    .D(in_5), .en(decoder_1_out15), .clk(in_3), .Q(out_21), .clr(in_4));
endmodule

module B_Changer (
  input  [15:0] DATA,
  input  [15:0] Change_bit,
  input  C_type,
  output [15:0] OUT
);

  wire [15:0] and_1_out, not_1_out, or_1_out;

  assign and_1_out = DATA & not_1_out;  // AND_Gate and_1, 16 bits wide
  assign not_1_out = ~Change_bit;  // NOT_Gate not_1, 16 bits wide
  assign or_1_out = DATA | Change_bit;  // OR_Gate or_1, 16 bits wide
  Multiplexer #(.width(16), .enable("false")) multiplexer_1 (.in0(and_1_out), .in1(or_1_out), .out(OUT), .sel(C_type));
endmodule

module LCD_CONTROLLER_2 (
);

  reg_16x16 reg_16x16_1 ();  // open: in_1, in_2, in_3, in_4, in_5, out_6, out_7, out_8, out_9, out_10, out_11, out_12, out_13, out_14, out_15, out_16, out_17, out_18, out_19, out_20, out_21
endmodule

module main3 (
  input  [31:0] in_1,
  input  in_2,
  input  in_3,
  input  in_4
);

  wire clock_1_out, clock_2_out, comparator_1_eq, cpu_16b_1_meme, cpu_16b_1_mw;
  wire [15:0] cpu_16b_1_mema, cpu_16b_1_out_5, cpu_16b_1_pc, reg_16x16_1_out_6, reg_16x16_1_out_7,
       reg_16x16_1_out_8, reg_16x16_1_out_9, reg_16x16_1_out_10, reg_16x16_1_out_11, reg_16x16_1_out_12,
       reg_16x16_1_out_13, reg_16x16_1_out_14, reg_16x16_1_out_15, reg_16x16_1_out_16, reg_16x16_1_out_17,
       reg_16x16_1_out_18, reg_16x16_1_out_19, reg_16x16_1_out_20, reg_16x16_1_out_21;
  wire [31:0] multiplexer_1_out, rom_1_data;

  Register register_1 ();  // open: D, en, Q, clk, clr
  Clock clock_1 (.out(clock_1_out));
  Multiplexer #(.width(32), .enable("false")) multiplexer_1 (
    .in0(rom_1_data), .in1(in_1), .out(multiplexer_1_out), .sel(in_2));
  ROM #(.addrWidth(16), .dataWidth(32)) rom_1 (.addr(cpu_16b_1_pc), .data(rom_1_data));
  CPU_16b cpu_16b_1 (
    .INSTRUCTION(multiplexer_1_out), .CLK(clock_1_out), .RST(in_4), .MEMA(cpu_16b_1_mema), .PC(cpu_16b_1_pc),
    .MW(cpu_16b_1_mw), .MEME(cpu_16b_1_meme), .out_5(cpu_16b_1_out_5));
  RAM #(.addrWidth(16), .dataWidth(16)) ram_1 (
    .addr(cpu_16b_1_mema), .we(cpu_16b_1_mw), .oe(cpu_16b_1_meme), .clk(clock_1_out), .data(cpu_16b_1_out_5));
  DotMatrix #(.matrixcols(16), .matrixrows(16)) dotmatrix_1 (
    .col0(reg_16x16_1_out_6), .col1(reg_16x16_1_out_10), .col2(reg_16x16_1_out_14),
    .col3(reg_16x16_1_out_18), .col4(reg_16x16_1_out_7), .col5(reg_16x16_1_out_11),
    .col6(reg_16x16_1_out_15), .col7(reg_16x16_1_out_19), .col8(reg_16x16_1_out_8),
    .col9(reg_16x16_1_out_12), .col10(reg_16x16_1_out_16), .col11(reg_16x16_1_out_20),
    .col12(reg_16x16_1_out_9), .col13(reg_16x16_1_out_13), .col14(reg_16x16_1_out_17),
    .col15(reg_16x16_1_out_21));
  reg_16x16 reg_16x16_1 (
    .in_1(comparator_1_eq), .in_2(cpu_16b_1_mema[3:0]), .in_3(clock_2_out), .in_5(cpu_16b_1_out_5),
    .out_6(reg_16x16_1_out_6), .out_7(reg_16x16_1_out_7), .out_8(reg_16x16_1_out_8),
    .out_9(reg_16x16_1_out_9), .out_10(reg_16x16_1_out_10), .out_11(reg_16x16_1_out_11),
    .out_12(reg_16x16_1_out_12), .out_13(reg_16x16_1_out_13), .out_14(reg_16x16_1_out_14),
    .out_15(reg_16x16_1_out_15), .out_16(reg_16x16_1_out_16), .out_17(reg_16x16_1_out_17),
    .out_18(reg_16x16_1_out_18), .out_19(reg_16x16_1_out_19), .out_20(reg_16x16_1_out_20),
    .out_21(reg_16x16_1_out_21));  // open: in_4
  Clock clock_2 (.out(clock_2_out));
  Comparator #(.width(12)) comparator_1 (
    .a(cpu_16b_1_mema[15:4]), .b({12{1'b1}}), .eq(comparator_1_eq));  // open: gt, lt

  // Notes on the sheet:
  //   contents of rom_1 (hex, n*v repeats v):
  //   818b0007 c180fff0
endmodule
